# Fritzing sketch IOT Crop Production (saved by Fritzing 0.9.3b)
breadboards: 1

parts:
  WeMos_D1_Mini1 = WeMos D1 Mini
  Part1 = Soil Moisture Sensor
  Part2 = Humidity Temperature Sensor SHT15
  BAT1 = Battery Holders [package=lipo-1100mAh]  # not connected

nets:
  VCC: WeMos_D1_Mini1.5V, Part1.VCC, Part2.VCC
  N1: WeMos_D1_Mini1.D1, Part1.SIG
  N2: WeMos_D1_Mini1.D2, Part2.SDA
  GND: WeMos_D1_Mini1.G, Part1.GND, Part2.GND
